# Fritzing sketch blink (saved by Fritzing 0.9.3b)
breadboards: 1

parts:
  U1 = atmega168 [package=dip]
  C1 = Ceramic Capacitor [capacitance=100nF package="100 mil [THT, multilayer]"]
  R1 = Resistor [tolerance=±5% resistance=220 package=THT]
  LED1 = LED - 5mm [color="Green (555nm)" package="5 mm [THT]"]

nets:
  N1: U1.VCC, C1.0
  N2: U1.GND#7, C1.1, R1.Pin_1
  N3: U1.D8, R1.Pin_0, LED1.cathode, LED1.anode
