# Fritzing sketch segment7 (saved by Fritzing 0.9.3b)
breadboards: 1

parts:
  U1 = atmega168 [package=dip]
  C1 = Ceramic Capacitor [capacitance=100nF package="100 mil [THT, multilayer]"]
  R1 = Resistor [tolerance=±5% resistance=220 package=THT]
  R2 = Resistor [tolerance=±5% resistance=220 package=THT]
  Part2 = 0.56" 7-segment LED Backpack [part_number=879]

nets:
  VCC: U1.VCC, C1.0, R1.Pin_0, R2.Pin_0, Part2.VDD
  N1: U1.GND#7, C1.1, Part2.GND
  N2: U1.A4, R2.Pin_1, Part2.SDA
  N3: U1.A5, R1.Pin_1, Part2.SCL

custom parts:
  0.56" 7-segment LED Backpack: This 0.56" 7-segment LED display includes a driver chip for simple control via an I2C interface. The backpack features address-selection jumpers so you can connect up to eight displays on a single I2C bus.
