# Fritzing sketch lfsr (saved by Fritzing 0.9.3b)
breadboards: 1

parts:
  U1 = atmega168 [package=dip]
  C1 = Ceramic Capacitor [capacitance=100nF package="100 mil [THT, multilayer]"]
  Part1 = Mini 8x8 LED Matrix Backpack [part_number=870]
  R1 = Resistor [tolerance=±5% resistance=220 package=THT]
  R2 = Resistor [tolerance=±5% resistance=220 package=THT]
  LED1 = LED - 5mm [color="Green (555nm)" package="5 mm [THT]"]
  R3 = Resistor [tolerance=±5% resistance=220 package=THT]

nets:
  VCC: U1.VCC, C1.0, Part1.VDD, R1.Pin_0, R2.Pin_0
  N1: U1.GND#7, C1.1, Part1.GND
  N2: U1.D8, LED1.cathode
  N3: U1.A4, Part1.SDA, R2.Pin_1
  N4: U1.A5, Part1.SCL, R1.Pin_1
  N5: LED1.anode, R3.Pin_0

custom parts:
  Mini 8x8 LED Matrix Backpack: This 0.8" 8x8 monochrome LED matrix includes a driver chip for simple control via an I2C interface. The backpack features address-selection jumpers so you can connect up to four matrices on a single I2C bus.
